// Logisim project projet.circ as structural Verilog: 18 circuits, main circuit main
module main (
  input  [3:0] Data_in,
  input  Sel,
  input  [1:0] Reg_sel,
  input  CLK,
  input  [1:0] sel_MUX_y,
  input  RESET,
  input  [1:0] sel_MUX_x,
  input  Sely,
  input  Selx,
  input  [2:0] sel_op,
  output [3:0] Data_out
);

  wire [3:0] banc_de_registre_1_out_x, banc_de_registre_1_out_y;

  banc_de_registre banc_de_registre_1 (
    .Data(Data_in), .Sel(Sel), .register_sel(Reg_sel), .SelY(Sely), .out_X(banc_de_registre_1_out_x),
    .out_Y(banc_de_registre_1_out_y), .CLK(CLK), .Reset(RESET), .Sel_MUX_1(sel_MUX_x), .Sel_MUX_2(sel_MUX_y),
    .SelX(Selx));
  // alu_4bit alu_4bit_1: pin names not known; wires that end beside it: sel_op, banc_de_registre_1_out_y, Data_out, banc_de_registre_1_out_x
endmodule

module full_adder (
  input  Rin,
  input  A,
  input  B,
  output S,
  output Rout
);

  wire and_1_out, and_2_out, xor_1_out;

  xor xor_1 (xor_1_out, A, B);
  xor xor_2 (S, xor_1_out, Rin);
  and and_1 (and_1_out, xor_1_out, Rin);
  and and_2 (and_2_out, A, B);
  or or_1 (Rout, and_2_out, and_1_out);
endmodule

// register bench
module banc_de_registre (
  input  [3:0] Data,
  input  Sel,
  input  [1:0] register_sel,
  input  CLK,
  input  Reset,
  input  SelX,
  input  SelY,
  input  [1:0] Sel_MUX_1,
  input  [1:0] Sel_MUX_2,
  output [3:0] out_X,
  output [3:0] out_Y
);

  wire and_1_out, and_2_out, and_3_out, and_4_out, decodeur_1_out_2, decodeur_1_out_3, decodeur_1_out_4,
       decodeur_1_out_5;
  wire [3:0] register_1_outx, register_1_outy, register_2_outx, register_2_outy, register_3_outx,
       register_3_outy, register_4_outx, register_4_outy;

  decodeur decodeur_1 (
    .in_1(register_sel), .out_2(decodeur_1_out_2), .out_3(decodeur_1_out_3), .out_4(decodeur_1_out_4),
    .out_5(decodeur_1_out_5));
  and and_1 (and_1_out, Sel, decodeur_1_out_2);
  and and_2 (and_2_out, Sel, decodeur_1_out_3);
  and and_3 (and_3_out, Sel, decodeur_1_out_4);
  and and_4 (and_4_out, Sel, decodeur_1_out_5);
  register register_1 (
    .In(Data), .wA(and_1_out), .CLK(CLK), .rA1(SelX), .rA2(SelY), .Reset(Reset), .outX(register_1_outx),
    .outY(register_1_outy));
  register register_2 (
    .In(Data), .wA(and_2_out), .CLK(CLK), .rA1(SelX), .rA2(SelY), .Reset(Reset), .outX(register_2_outx),
    .outY(register_2_outy));
  register register_3 (
    .In(Data), .wA(and_3_out), .CLK(CLK), .rA1(SelX), .rA2(SelY), .Reset(Reset), .outX(register_3_outx),
    .outY(register_3_outy));
  register register_4 (
    .In(Data), .wA(and_4_out), .CLK(CLK), .rA1(SelX), .rA2(SelY), .Reset(Reset), .outX(register_4_outx),
    .outY(register_4_outy));
  mux4_4bit mux4_4bit_1 (
    .OUT(out_X), .in0(register_1_outx), .in1(register_2_outx), .in2(register_3_outx), .in3(register_4_outx),
    .sel(Sel_MUX_1));
  mux4_4bit mux4_4bit_2 (
    .OUT(out_Y), .in0(register_1_outy), .in1(register_2_outy), .in2(register_3_outy), .in3(register_4_outy),
    .sel(Sel_MUX_2));
endmodule

// DEC
module decodeur (
  input  [1:0] in_1,
  output out_2,
  output out_3,
  output out_4,
  output out_5
);

  wire not_1_out, not_2_out, not_3_out, not_4_out;

  not not_1 (not_1_out, in_1[1]);
  not not_2 (not_2_out, in_1[0]);
  not not_3 (not_3_out, in_1[1]);
  not not_4 (not_4_out, in_1[0]);
  and and_1 (out_2, not_1_out, not_2_out);
  and and_2 (out_3, not_3_out, in_1[0]);
  and and_3 (out_4, in_1[1], not_4_out);
  and and_4 (out_5, in_1[1], in_1[0]);
endmodule

// MUX
module multiplexeur_8_1bit____1 (
  input  D0,
  input  D1,
  input  D2,
  input  D3,
  input  D4,
  input  D5,
  input  D6,
  input  D7,
  input  [2:0] in_9,
  output out_10
);

  wire and_1_out, and_2_out, and_3_out, and_4_out, and_5_out, and_6_out, and_7_out, and_8_out, not_1_out,
       not_2_out, not_3_out;

  not not_1 (not_1_out, in_9[2]);
  not not_2 (not_2_out, in_9[1]);
  not not_3 (not_3_out, in_9[0]);
  and and_1 (and_1_out, D0, not_1_out, not_2_out, not_3_out);
  and and_2 (and_2_out, D1, not_1_out, not_2_out, in_9[0]);
  and and_3 (and_3_out, D2, not_1_out, in_9[1], not_3_out);
  and and_4 (and_4_out, D3, not_1_out, in_9[1], in_9[0]);
  and and_5 (and_5_out, D4, in_9[2], not_2_out, not_3_out);
  and and_6 (and_6_out, D5, in_9[2], not_2_out, in_9[0]);
  and and_7 (and_7_out, D6, in_9[2], in_9[1], not_3_out);
  and and_8 (and_8_out, D7, in_9[2], in_9[1], in_9[0]);
  or or_1 (out_10, and_1_out, and_2_out, and_3_out, and_4_out, and_5_out, and_6_out, and_7_out, and_8_out);
endmodule

module register (
  input  [3:0] In,
  input  wA,
  input  CLK,
  input  rA1,
  input  rA2,
  input  Reset,
  output [3:0] outX,
  output [3:0] outY
);

  wire controlled_buffer_1_out, controlled_buffer_2_out, controlled_buffer_3_out, controlled_buffer_4_out,
       d_ff_1_q, d_ff_2_q, d_ff_3_q, d_ff_4_q;

  assign controlled_buffer_1_out = wA ? In[1] : 1'bz;  // Controlled_Buffer controlled_buffer_1
  assign controlled_buffer_2_out = wA ? In[2] : 1'bz;  // Controlled_Buffer controlled_buffer_2
  assign controlled_buffer_3_out = wA ? In[3] : 1'bz;  // Controlled_Buffer controlled_buffer_3
  assign controlled_buffer_4_out = wA ? In[0] : 1'bz;  // Controlled_Buffer controlled_buffer_4
  D_Flip_Flop d_ff_1 (.clk(CLK), .D(controlled_buffer_4_out), .Q(d_ff_1_q), .reset(Reset));  // open: Qn, preset, en
  D_Flip_Flop d_ff_2 (.clk(CLK), .D(controlled_buffer_1_out), .Q(d_ff_2_q), .reset(Reset));  // open: Qn, preset, en
  D_Flip_Flop d_ff_3 (.clk(CLK), .D(controlled_buffer_2_out), .Q(d_ff_3_q), .reset(Reset));  // open: Qn, preset, en
  D_Flip_Flop d_ff_4 (.clk(CLK), .D(controlled_buffer_3_out), .Q(d_ff_4_q), .reset(Reset));  // open: Qn, preset, en
  assign outY[0] = rA2 ? d_ff_1_q : 1'bz;  // Controlled_Buffer controlled_buffer_5
  assign outY[1] = rA2 ? d_ff_2_q : 1'bz;  // Controlled_Buffer controlled_buffer_6
  assign outY[2] = rA2 ? d_ff_3_q : 1'bz;  // Controlled_Buffer controlled_buffer_7
  assign outX[0] = rA1 ? d_ff_1_q : 1'bz;  // Controlled_Buffer controlled_buffer_8
  assign outX[1] = rA1 ? d_ff_2_q : 1'bz;  // Controlled_Buffer controlled_buffer_9
  assign outX[2] = rA1 ? d_ff_3_q : 1'bz;  // Controlled_Buffer controlled_buffer_10
  assign outY[3] = rA2 ? d_ff_4_q : 1'bz;  // Controlled_Buffer controlled_buffer_11
  assign outX[3] = rA1 ? d_ff_4_q : 1'bz;  // Controlled_Buffer controlled_buffer_12
endmodule

// Flip Flop
module basule_D_flip_flop (
  input  In,
  input  CLK,
  output Q,
  output Q_prime
);

  wire nand_1_out, nand_2_out, not_1_out;

  not not_1 (not_1_out, In);
  nand nand_1 (nand_1_out, In, CLK);
  nor nor_1 (Q, nand_1_out, Q_prime);
  nor nor_2 (Q_prime, Q, nand_2_out);
  nand nand_2 (nand_2_out, CLK, not_1_out);
endmodule

module alu_1bit (
  input  C_in,
  input  A,
  input  B,
  input  [2:0] Select,
  output Result,
  output out_6
);

  wire and_1_out, and_2_out, and_3_out, and_4_out, and_5_out, and_6_out, and_7_out, and_8_out, and_9_out,
       decodeur_3bit_1_s0, decodeur_3bit_1_s1, decodeur_3bit_1_s2, decodeur_3bit_1_s3, decodeur_3bit_1_s4,
       decodeur_3bit_1_s5, decodeur_3bit_1_s6, decodeur_3bit_1_s7, full_adder_1_s, nand_1_out, nor_1_out,
       not_1_out, not_2_out, or_1_out, xor_1_out;

  and and_1 (and_1_out, A, B);
  or or_1 (or_1_out, A, B);
  not not_1 (not_1_out, B);
  full_adder full_adder_1 (.A(A), .B(B), .S(full_adder_1_s), .Rin(C_in), .Rout(out_6));
  xor xor_1 (xor_1_out, A, B);
  not not_2 (not_2_out, A);
  nand nand_1 (nand_1_out, A, B);
  nor nor_1 (nor_1_out, A, B);
  decodeur_3bit decodeur_3bit_1 (
    .F2(Select[2]), .F1(Select[1]), .F0(Select[0]), .s0(decodeur_3bit_1_s0), .s1(decodeur_3bit_1_s1),
    .s2(decodeur_3bit_1_s2), .s3(decodeur_3bit_1_s3), .s4(decodeur_3bit_1_s4), .s5(decodeur_3bit_1_s5),
    .s6(decodeur_3bit_1_s6), .s7(decodeur_3bit_1_s7));
  and and_2 (and_2_out, and_1_out, decodeur_3bit_1_s0);
  and and_3 (and_3_out, or_1_out, decodeur_3bit_1_s1);
  and and_4 (and_4_out, not_1_out, decodeur_3bit_1_s2);
  and and_5 (and_5_out, full_adder_1_s, decodeur_3bit_1_s3);
  and and_6 (and_6_out, xor_1_out, decodeur_3bit_1_s4);
  and and_7 (and_7_out, not_2_out, decodeur_3bit_1_s5);
  and and_8 (and_8_out, nand_1_out, decodeur_3bit_1_s6);
  and and_9 (and_9_out, nor_1_out, decodeur_3bit_1_s7);
  or or_2 (Result, and_2_out, and_3_out, and_4_out, and_5_out, and_6_out, and_7_out, and_8_out, and_9_out);
endmodule

// DEC 3bit
module decodeur_3bit (
  input  F2,
  input  F1,
  input  F0,
  output s0,
  output s1,
  output s2,
  output s3,
  output s4,
  output s5,
  output s6,
  output s7
);

  wire not_1_out, not_2_out, not_3_out;

  not not_1 (not_1_out, F2);
  not not_2 (not_2_out, F1);
  not not_3 (not_3_out, F0);
  and and_1 (s0, not_2_out, not_3_out, not_1_out);
  and and_2 (s1, not_2_out, F0, not_1_out);
  and and_3 (s2, F1, not_3_out, not_1_out);
  and and_4 (s3, F1, F0, not_1_out);
  and and_5 (s4, not_2_out, not_3_out, F2);
  and and_6 (s5, F2, F0, not_2_out);
  and and_7 (s6, F2, not_3_out, F1);
  and and_8 (s7, F2, F0, F1);
endmodule

// ALU 4bit
module alu_4bit (
  input  C_in,
  input  [3:0] Ai,
  input  [3:0] Bi,
  input  [2:0] sel,
  output [3:0] OUT,
  output C_out
);

  wire alu_1bit_1_out_6, alu_1bit_2_out_6, alu_1bit_3_out_6;

  alu_1bit alu_1bit_1 (.A(Ai[0]), .B(Bi[0]), .Select(sel), .C_in(C_in), .out_6(alu_1bit_1_out_6), .Result(OUT[0]));
  alu_1bit alu_1bit_2 (
    .A(Ai[1]), .B(Bi[1]), .Select(sel), .C_in(alu_1bit_1_out_6), .out_6(alu_1bit_2_out_6), .Result(OUT[1]));
  alu_1bit alu_1bit_3 (
    .A(Ai[2]), .B(Bi[2]), .Select(sel), .C_in(alu_1bit_2_out_6), .out_6(alu_1bit_3_out_6), .Result(OUT[2]));
  alu_1bit alu_1bit_4 (.A(Ai[3]), .B(Bi[3]), .Select(sel), .C_in(alu_1bit_3_out_6), .out_6(C_out), .Result(OUT[3]));
endmodule

// MUX8 1bit
module mux8_1bit (
  input  D0,
  input  D1,
  input  D2,
  input  D3,
  input  D4,
  input  D5,
  input  D6,
  input  D7,
  input  [2:0] in_9,
  output out_10
);

  wire and_1_out, and_2_out, and_3_out, and_4_out, and_5_out, and_6_out, and_7_out, and_8_out, not_1_out,
       not_2_out, not_3_out;

  not not_1 (not_1_out, in_9[1]);
  not not_2 (not_2_out, in_9[2]);
  not not_3 (not_3_out, in_9[0]);
  and and_1 (and_1_out, D0, not_2_out, not_1_out, not_3_out);
  and and_2 (and_2_out, D1, not_2_out, not_1_out, in_9[0]);
  and and_3 (and_3_out, D2, not_2_out, in_9[1], not_3_out);
  and and_4 (and_4_out, D3, not_2_out, in_9[1], in_9[0]);
  and and_5 (and_5_out, D4, in_9[2], not_1_out, not_3_out);
  and and_6 (and_6_out, D5, in_9[2], not_1_out, in_9[0]);
  and and_7 (and_7_out, D6, in_9[2], in_9[1], not_3_out);
  and and_8 (and_8_out, D7, in_9[2], in_9[1], in_9[0]);
  or or_1 (out_10, and_1_out, and_2_out, and_3_out, and_4_out, and_5_out, and_6_out, and_7_out, and_8_out);
endmodule

module mux8_4bit (
  input  [3:0] In_0,
  input  [3:0] In_1,
  input  [3:0] In_2,
  input  [3:0] In_3,
  input  [3:0] In_4,
  input  [3:0] In_5,
  input  [3:0] In_6,
  input  [3:0] In_7,
  input  [2:0] SEL,
  output [3:0] OUT
);

  mux8_1bit mux8_1bit_1 (
    .D0(In_0[0]), .D1(In_1[0]), .D2(In_2[0]), .D3(In_3[0]), .D4(In_4[0]), .D5(In_5[0]), .D6(In_6[0]),
    .D7(In_7[0]), .out_10(OUT[0]), .in_9(SEL));
  mux8_1bit mux8_1bit_2 (
    .D0(In_0[1]), .D1(In_1[1]), .D2(In_2[1]), .D3(In_3[1]), .D4(In_4[1]), .D5(In_5[1]), .D6(In_6[1]),
    .D7(In_7[1]), .out_10(OUT[1]), .in_9(SEL));
  mux8_1bit mux8_1bit_3 (
    .D0(In_0[2]), .D1(In_1[2]), .D2(In_2[2]), .D3(In_3[2]), .D4(In_4[2]), .D5(In_5[2]), .D6(In_6[2]),
    .D7(In_7[2]), .out_10(OUT[2]), .in_9(SEL));
  mux8_1bit mux8_1bit_4 (
    .D0(In_0[3]), .D1(In_1[3]), .D2(In_2[3]), .D3(In_3[3]), .D4(In_4[3]), .D5(In_5[3]), .D6(In_6[3]),
    .D7(In_7[3]), .out_10(OUT[3]), .in_9(SEL));
endmodule

// MUX4 1bit
module mux4_1bit (
  input  e0,
  input  e1,
  input  e2,
  input  e3,
  input  [1:0] sel,
  output S
);

  wire and_1_out, and_2_out, and_3_out, and_4_out, not_1_out, not_2_out;

  not not_1 (not_1_out, sel[1]);
  not not_2 (not_2_out, sel[0]);
  and and_1 (and_1_out, e0, not_1_out, not_2_out);
  and and_2 (and_2_out, e1, not_1_out, sel[0]);
  and and_3 (and_3_out, e2, sel[1], not_2_out);
  and and_4 (and_4_out, e3, sel[0], sel[1]);
  or or_1 (S, and_1_out, and_2_out, and_3_out, and_4_out);
endmodule

// MUX4 4bit
module mux4_4bit (
  input  [3:0] in0,
  input  [3:0] in1,
  input  [3:0] in2,
  input  [3:0] in3,
  input  [1:0] sel,
  output [3:0] OUT
);

  mux4_1bit mux4_1bit_1 (.e0(in0[0]), .e1(in1[0]), .e2(in2[0]), .e3(in3[0]), .S(OUT[0]), .sel(sel));
  mux4_1bit mux4_1bit_2 (.e0(in0[1]), .e1(in1[1]), .e2(in2[1]), .e3(in3[1]), .S(OUT[1]), .sel(sel));
  mux4_1bit mux4_1bit_3 (.e0(in0[2]), .e1(in1[2]), .e2(in2[2]), .e3(in3[2]), .S(OUT[2]), .sel(sel));
  mux4_1bit mux4_1bit_4 (.e0(in0[3]), .e1(in1[3]), .e2(in2[3]), .e3(in3[3]), .S(OUT[3]), .sel(sel));
endmodule

module Data_Path (
  input  [3:0] in_1,
  input  Register_write,
  input  [1:0] Destination,
  input  [1:0] X_out,
  input  [1:0] Y_out,
  input  selX,
  input  selY,
  input  CLK,
  input  RESET,
  input  [3:0] other_source_X,
  input  [3:0] other_source_Y,
  input  sel_Mux_X,
  input  sel_MUX_Y,
  input  [2:0] sel_ALU,
  output [3:0] out_15
);

  wire [3:0] banc_de_registre_1_out_x, banc_de_registre_1_out_y, mux2_4bit_1_out, mux2_4bit_2_out;

  banc_de_registre banc_de_registre_1 (
    .Data(in_1), .Sel(Register_write), .register_sel(Destination), .SelY(selY),
    .out_X(banc_de_registre_1_out_x), .out_Y(banc_de_registre_1_out_y), .CLK(CLK), .Reset(RESET),
    .Sel_MUX_1(X_out), .Sel_MUX_2(Y_out), .SelX(selX));
  mux2_4bit mux2_4bit_1 (
    .in_0(other_source_X), .OUT(mux2_4bit_1_out), .sel(sel_MUX_Y), .in_1(banc_de_registre_1_out_x));
  mux2_4bit mux2_4bit_2 (
    .in_0(other_source_Y), .OUT(mux2_4bit_2_out), .sel(sel_Mux_X), .in_1(banc_de_registre_1_out_y));
  alu_4bit alu_4bit_1 (.Ai(mux2_4bit_1_out), .Bi(mux2_4bit_2_out), .sel(sel_ALU), .OUT(out_15));  // open: C_in, C_out
endmodule

// MUX
module mux2_4bit (
  input  [3:0] in_0,
  input  [3:0] in_1,
  input  sel,
  output [3:0] OUT
);

  mux2_1bit mux2_1bit_1 (.e1(in_1[0]), .e0(in_0[0]), .S(OUT[0]), .SEL(sel));
  mux2_1bit mux2_1bit_2 (.e1(in_1[1]), .e0(in_0[1]), .S(OUT[1]), .SEL(sel));
  mux2_1bit mux2_1bit_3 (.e1(in_1[2]), .e0(in_0[2]), .S(OUT[2]), .SEL(sel));
  mux2_1bit mux2_1bit_4 (.e1(in_1[3]), .e0(in_0[3]), .S(OUT[3]), .SEL(sel));
endmodule

// MUX
module mux2_1bit (
  input  e1,
  input  e0,
  input  SEL,
  output S
);

  wire and_1_out, and_2_out, not_1_out;

  not not_1 (not_1_out, SEL);
  and and_1 (and_1_out, e1, SEL);
  and and_2 (and_2_out, e0, not_1_out);
  or or_1 (S, and_1_out, and_2_out);
endmodule

module control_unit (
  input  [11:0] in_1,
  output [3:0] OPCOD,
  output [1:0] RES,
  output [1:0] X,
  output [1:0] Y,
  output [1:0] EXT
);

  RAM ram_1 ();  // open: addr, data, sel, clk, ld, clr

  assign EXT = in_1[11:10];
  assign OPCOD = in_1[3:0];
  assign RES = in_1[5:4];
  assign X = in_1[7:6];
  assign Y = in_1[9:8];
endmodule
